# Fritzing sketch Master (saved by Fritzing 1.0.5)
circuit board: 22.943cm x 12.7266cm
breadboards: 3

parts:
  Part1 = LCD1602-I2C
  Sensor1 = Gas Sensor Breakout Board
  microSD1 = MicroSD Card Module
  GSM_SIM_GPSR_SMS_SIM900_SIM1 = SIM800L [package=THT]
  RHT1 = Humidity and Temperature Sensor RHT03
  A1 = PIR sensor (non-bendable legs)
  S1 = Pushbutton [package="[THT]"]
  S2 = Pushbutton [package="[THT]"]
  LED1 = LED - 5mm [color="Red (633nm)" current=0.030A package="5 mm [THT]"]
  LED2 = LED - 5mm [color="Green (565nm)" current=30mA package="5 mm [THT]"]  # not connected
  R1 = Resistor [tolerance=±5% power=0.25W resistance=220 package=THT]
  R2 = Resistor [tolerance=±5% power=0.25W resistance=220 package=THT]
  Mod3 = KY-018 Photoresistor Module [package="Breakout board"]
  Mod4 = KY-018 Photoresistor Module [package="Breakout board"]
  U1 = ESP32-38PinWide [part_number=ESP32-38PinWide]
  Laser_Sensor_Module1 = Laser Sensor Module [part_number="Laser Sensor Module" chip_label=IC package="DIP (Dual Inline) [THT]"]
  Laser_Sensor_Module2 = Laser Sensor Module [part_number="Laser Sensor Module" chip_label=IC package="DIP (Dual Inline) [THT]"]
  J1 = Piezo Speaker

nets:
  GND: Part1.GND, Sensor1.GND, microSD1.GND, GSM_SIM_GPSR_SMS_SIM900_SIM1.GND, RHT1.GND_1, A1.GND, S1.Pin_3, S1.Pin_4, S2.Pin_3, S2.Pin_4, LED1.cathode, Mod3.-, Mod4.-, U1.GND, Laser_Sensor_Module1.GND, Laser_Sensor_Module2.GND, J1.pin1
  VCC: Part1.VCC, Sensor1.5V, microSD1.VCC, GSM_SIM_GPSR_SMS_SIM900_SIM1.5V, RHT1.Vcc, A1.VDD, Mod3.Vin, Mod4.Vin, U1.VIN, Laser_Sensor_Module1.VCC, Laser_Sensor_Module2.VCC
  N1: Part1.SDA, U1.GPIO21
  N2: Part1.SCL, U1.GPIO22
  N3: Sensor1.AOUT, U1.GPIO32
  N4: microSD1.MISO, U1.GPIO19
  N5: microSD1.MOSI, U1.GPIO23
  N6: microSD1.SCK, U1.GPIO18
  N7: microSD1.CS, U1.GPIO5
  N8: GSM_SIM_GPSR_SMS_SIM900_SIM1.SIM_TXD, U1.GPIO17
  N9: GSM_SIM_GPSR_SMS_SIM900_SIM1.SIM_RXD, U1.GPIO16
  N10: RHT1.Data-signal, U1.GPIO25
  N11: A1.SIG, U1.GPIO26
  N12: S1.Pin_1, S1.Pin_2, U1.GPIO4
  N13: S2.Pin_1, S2.Pin_2, U1.GPIO13
  N14: LED1.anode, R2.Pin_0
  N15: R1.Pin_1, U1.GPIO14
  N16: R2.Pin_1, U1.GPIO12
  N17: Mod3.S, U1.GPIO34
  N18: Mod4.S, U1.GPIO35
  N19: U1.GPIO27, J1.pin2

custom parts:
  LCD1602-I2C: A standard character display, usually with 2x16 characters. Comes in many colors with LCM1602 IIC attached.
  Gas Sensor Breakout Board: Gas sensor breakout board. Input voltage is 5V. Sensor output is available in analog and digital.
  PIR sensor (non-bendable legs): Generic PIR sensor
  KY-018 Photoresistor Module: KY-018 Photoresistor module, used to measure light intensity. It can determine the presence or absence of light.
  ESP32-38PinWide: Generic 38-Pin ESP32 with wide format (only access to one side of pins on a breadboard) based on Stephen Lilley's HiLetgo ESP-WROOM-32 ESP32 ESP-32S Development Board.
  Laser Sensor Module: Laser Sensor/Detector/Receiver Module Working Voltage: 5V
