# Fritzing sketch Water_Tank (saved by Fritzing 1.0.5)
breadboards: 2

parts:
  Part1 = SRF05 Ultrasonic Rangefinder
  U1 = ESP32-38PinWide [part_number=ESP32-38PinWide]

nets:
  VCC: Part1.VCC, U1.VIN
  N1: Part1.Trig, U1.GPIO5
  N2: Part1.Echo, U1.GPIO18
  GND: Part1.GND, U1.GND

custom parts:
  ESP32-38PinWide: Generic 38-Pin ESP32 with wide format (only access to one side of pins on a breadboard) based on Stephen Lilley's HiLetgo ESP-WROOM-32 ESP32 ESP-32S Development Board.
